# Fritzing sketch no-computer (saved by Fritzing 0.9.10b)
breadboards: 1

parts:
  Part1 = 16 NeoPixel Ring [part_number=1463]
  Part2 = Adafruit Metro Without Headers [part_number="Adafruit #2466"]
  R1 = Resistor [tolerance=±5% power=0.25 resistance=100000 package=THT]
  VCC1 = Battery

nets:
  N1: Part1.IN, Part2.IO2
  VDD: Part1.VDD, Part2.+5V, VCC1.+
  GND: Part1.GND, Part2.GND, VCC1.-
  N2: Part2.MOSI, R1.Pin_1
  N3: Part2.IO8, R1.Pin_0

custom parts:
  16 NeoPixel Ring: 16 ultra bright smart LED NeoPixels are arranged in a circle with 1.75" (44.5mm) outer diameter. The rings are 'chainable' - connect the output pin of one to the input pin of another. Use only one microcontroller pin to control as many as you can chain together! Each LED is addressable as the driver chip is inside the LED. Each one has ~18mA constant current drive so the color will be very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
  Adafruit Metro Without Headers: We sure love the ATmega328 here at Adafruit, and we use them a lot for our own projects. The processor has plenty of GPIO, Analog inputs, hardware UART SPI and I2C, timers and PWM galore - just enough for most simple projects. When we need to go small, we use a Pro Trinket 3V or 5V, but when size isn't as much of a concern, and a USB-serial converter is required, we reach for an Adafruit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
